# Fritzing sketch ESP32-4x8x8 dot matrix led max7219 (saved by Fritzing 0.9.3b)
breadboards: 1

parts:
  U1 = ESP32S-HiLetgo [part_number=ESP32S-HiLetgo]
  Composant1 = LED Matrix - Serial Interface - Red/Green/Blue
  J1 = Power Jack [package=power_jack_pth_lock]  # not connected

nets:
  N1: U1.GPIO14, Composant1.VCC
  N2: U1.GPIO12, Composant1.CS
  GND: U1.GND, U1.VIN, Composant1.MISO, Composant1.GND, Composant1.MOSI
  N3: U1.GPIO15, Composant1.SCK

notes:
  D15
  GND
  VIN
  D12
  D14
  VCC
  GND
  DIN
  CS
  CLK
  Female barrel jack
  4x 8x8 dot matrix chained
  ESP32

custom parts:
  ESP32S-HiLetgo: HiLetgo ESP-WROOM-32 ESP32 ESP-32S Development Board 2.4GHz Dual-Mode WiFi + Bluetooth Dual Cores Microcontroller The ESP32 integrated with Antenna switches, RF Balun, power amplifiers, low-noise amplifiers, filters, and management modules, and the entire solution occupies the least area of PCB. 2.4 GHz Wi-Fi plus Bluetooth dual-mode chip, with TSMC Ultra-low power consumption 40nm technology,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
