# Fritzing sketch controler-board (saved by Fritzing 0.9.3b)
breadboards: 1

parts:
  Composant1 = Arduino Nano (Rev3.0)
  Q1 = NPN-Transistor [package="SOT-23 [SMD]"]
  S1 = Taiway 100-SP-X-T1 SPDT Miniature Toggle Switch [part_number=100-SP-X-T1-0-0-B1-M2 package=THT]
  R1 = Resistor [tolerance=±5% resistance=220 package="0603 [SMD]"]
  C1 = Ceramic Capacitor [capacitance=100nF package="200 mil [THT, multilayer]"]

nets:
  N1: Composant1.GND, Q1.0
  N2: Composant1.D3, Q1.1, R1.Pin_1
  N3: Composant1.D6, S1.L1, C1.1
  N4: Composant1.5V, Q1.2, S1.L2, R1.Pin_0, C1.0
