# Fritzing sketch motor-board (saved by Fritzing 0.9.3b)
breadboards: 1

parts:
  M1 = DC Motor
  J1 = ATX24 Pin Power Supply Connector [package=atx24_right_angle]
  Composant2 = Arduino Nano (Rev3.0) (ICSP)
  Composant1 = Monster Moto Shield
  Q2 = NPN-Transistor [package="SOT-23 [SMD]"]
  Q3 = NPN-Transistor [package="SOT-23 [SMD]"]
  Q4 = NPN-Transistor [package="SOT-23 [SMD]"]
  Q5 = NPN-Transistor [package="SOT-23 [SMD]"]
  R2 = Resistor [tolerance=±5% resistance=220 package="0603 [SMD]"]
  R3 = Resistor [tolerance=±5% resistance=220 package="0603 [SMD]"]
  R4 = Resistor [tolerance=±5% resistance=220 package="0603 [SMD]"]
  R5 = Resistor [tolerance=±5% resistance=220 package="0603 [SMD]"]
  RE1 = Rotary Encoder [package=THT]
  U1 = 7-SEGMENT-DISPLAY-1_-RED [package=7-segment-1_pth]

nets:
  N1: M1.pin_1, Composant1.OUTA1
  N2: M1.pin_2, Composant1.OUTB1
  12V: J1.12V, Composant1.VCC
  GND: J1.GND, Composant2.GND, Composant1.GND, Composant1.GND_-_GND@1, Q2.0, Q3.0, Q4.0, Q5.0, U1.D
  N3: Composant2.D2, RE1.EncoderPinB
  N4: Composant2.D3, RE1.EncoderPinC
  N5: Composant2.D4, RE1.EncoderPinA
  N6: Composant2.D5, Composant1.PWM1_-_D5
  N7: Composant2.D7, Composant1.INA1_-_D7
  N8: Composant2.D8, Composant1.INB1_-_D8
  N9: Composant2.D9, U1.DP
  N10: Composant2.D10, U1.C
  N11: Composant2.D11/MOSI, U1.G1
  5V: Composant2.5V, Composant1.5V, Q2.2, Q3.2, Q4.2, Q5.2, R2.Pin_0, R3.Pin_0, R4.Pin_0, R5.Pin_0
  N12: Composant2.A6, Composant1.EN1_-_A0
  N13: Composant2.A5, Composant1.CS1_-_A2
  N14: Composant2.A4, Q5.1, R5.Pin_1
  N15: Composant2.A3, Q4.1, R4.Pin_1
  N16: Composant2.A2, Q3.1, R3.Pin_1
  N17: Composant2.A1, Q2.1, R2.Pin_1

notes:
  VNH2SP30 board
  (single, not dual motor
  board)
  ATX 12V power supply
  One A3144 hall sensor
  per dust collection line
  Rotary
  encoder:
  VCC,SW, INT,INT0,
  GND
  8 digits
  7 segments
  VCC, GND,DIN,CS,CLK
