# Fritzing sketch LuminousFrameFritzing (saved by Fritzing 0.9.3b)

parts:
  Composant1 = Arduino Leonardo (Rev3b)
  LED1 = LED - 5mm [color="Red (633nm)" package="5 mm [THT]"]  # not connected
  LED2 = LED - 5mm [color="Red (633nm)" package="5 mm [THT]"]  # not connected
  LED3 = LED - 5mm [color="Red (633nm)" package="5 mm [THT]"]  # not connected
  LED4 = LED - 5mm [color="Red (633nm)" package="5 mm [THT]"]  # not connected
  LED5 = LED - 5mm [color="Red (633nm)" package="5 mm [THT]"]  # not connected
  LED6 = LED - 5mm [color="Red (633nm)" package="5 mm [THT]"]
  LED7 = LED - 5mm [color="Red (633nm)" package="5 mm [THT]"]  # not connected
  LED8 = LED - 5mm [color="Red (633nm)" package="5 mm [THT]"]  # not connected
  LED9 = LED - 5mm [color="Red (633nm)" package="5 mm [THT]"]
  LED10 = LED - 5mm [color="Red (633nm)" package="5 mm [THT]"]  # not connected
  LED11 = LED - 5mm [color="Red (633nm)" package="5 mm [THT]"]  # not connected
  LED12 = LED - 5mm [color="Red (633nm)" package="5 mm [THT]"]  # not connected
  LED13 = LED - 5mm [color="Red (633nm)" package="5 mm [THT]"]  # not connected
  LED14 = LED - 5mm [color="Red (633nm)" package="5 mm [THT]"]  # not connected
  LCD1 = LCD screen
  U1 = 74HC595 [package="DIP16 [THT]"]
  U2 = 74HC595 [package="DIP16 [THT]"]
  R1 = Resistor [tolerance=±5% resistance=220 package=THT]  # not connected
  R2 = Resistor [tolerance=±5% resistance=220 package=THT]  # not connected
  R3 = Resistor [tolerance=±5% resistance=220 package=THT]  # not connected
  R4 = Resistor [tolerance=±5% resistance=220 package=THT]  # not connected
  R5 = Resistor [tolerance=±5% resistance=220 package=THT]  # not connected
  R6 = Resistor [tolerance=±5% resistance=220 package=THT]  # not connected
  R7 = Resistor [tolerance=±5% resistance=220 package=THT]  # not connected
  R8 = Resistor [tolerance=±5% resistance=220 package=THT]  # not connected
  LED15 = LED - 5mm [color="Red (633nm)" package="5 mm [THT]"]  # not connected
  LED16 = LED - 5mm [color="Red (633nm)" package="5 mm [THT]"]  # not connected
  R9 = Resistor [tolerance=±5% resistance=220 package=THT]  # not connected
  R10 = Resistor [tolerance=±5% resistance=220 package=THT]  # not connected
  R11 = Resistor [tolerance=±5% resistance=220 package=THT]  # not connected
  R12 = Resistor [tolerance=±5% resistance=220 package=THT]  # not connected
  R13 = Resistor [tolerance=±5% resistance=220 package=THT]  # not connected
  R15 = Resistor [tolerance=±5% resistance=220 package=THT]  # not connected
  R16 = Resistor [tolerance=±5% resistance=220 package=THT]  # not connected
  R17 = Resistor [tolerance=±5% resistance=220 package=THT]  # not connected
  C2 = Tantalum Capacitor [capacitance=1μF package="100 mil [THT, tantalum]"]

nets:
  N1: Composant1.D0/RX, LCD1.V0
  N2: Composant1.D1/TX, LCD1.RS
  VCC: Composant1.5V, LCD1.VDD, U1.MR, U1.VCC, U2.MR, U2.VCC
  GND: Composant1.GND, U1.GND, U1.OE, U2.GND, C2.-
  N3: Composant1.A2, U1.DS
  N4: Composant1.A4, U2.ST_CP
  N5: Composant1.A5, U2.SH_CP
  N6: LED6.anode, LED9.anode
  N7: U1.Q7', U2.DS

notes:
  Serial LCD Module LCD09395
  LEDS (to point at x,y in photo frame)
  (2x8)
  SHIFT BIT REGISTER
  74HC595 (x2)
  ARDUINO LEONARDO
  RESISTOR 220ohms
  (2x8)
  CONDENSATEUR
  1uF
