# Fritzing sketch Sweet Dreams (saved by Fritzing 0.9.3b)
breadboards: 1

parts:
  Composant1 = Arduino Nano (Rev3.0)
  RGB_SMD_LED1 = SMD RGB LED (WS2812) [package=5050]

nets:
  GND: Composant1.GND, RGB_SMD_LED1.VSS
  N1: Composant1.D6, RGB_SMD_LED1.DIn
  5V: Composant1.5V, RGB_SMD_LED1.VCC
